// Logisim project Adder&Subtractor.circ as structural Verilog
module HalfAdder (
  input  in_1,
  input  in_2,
  output out_3,
  output out_4
);

  xor xor_1 (out_3, in_1, in_2);
  and and_1 (out_4, in_1, in_2);
endmodule

module FullAdder (
  input  in_1,
  input  in_2,
  input  in_3,
  output out_4,
  output out_5
);

  wire halfadder_1_out_3, halfadder_1_out_4, halfadder_2_out_4;

  HalfAdder halfadder_1 (.in_1(in_1), .in_2(in_2), .out_3(halfadder_1_out_3), .out_4(halfadder_1_out_4));
  HalfAdder halfadder_2 (.in_1(halfadder_1_out_3), .in_2(in_3), .out_3(out_4), .out_4(halfadder_2_out_4));
  or or_1 (out_5, halfadder_2_out_4, halfadder_1_out_4);
endmodule

module Parallel_Full_Adder (
  input  in_1,
  input  in_2,
  input  in_3,
  input  in_4,
  input  in_5,
  input  in_6,
  input  in_7,
  input  in_8,
  input  in_9,
  output out_10,
  output out_11,
  output out_12,
  output out_13,
  output out_14
);

  wire fulladder_1_out_5, fulladder_2_out_5, fulladder_3_out_5;

  FullAdder fulladder_1 (.in_1(in_2), .in_2(in_3), .in_3(in_1), .out_4(out_10), .out_5(fulladder_1_out_5));
  FullAdder fulladder_2 (.in_1(in_4), .in_2(in_5), .in_3(fulladder_1_out_5), .out_4(out_11), .out_5(fulladder_2_out_5));
  FullAdder fulladder_3 (.in_1(in_6), .in_2(in_7), .in_3(fulladder_2_out_5), .out_4(out_12), .out_5(fulladder_3_out_5));
  FullAdder fulladder_4 (.in_1(in_8), .in_2(in_9), .in_3(fulladder_3_out_5), .out_4(out_13), .out_5(out_14));
endmodule

module Addition_Subtraction (
  input  Mode,
  input  a0,
  input  a1,
  input  a2,
  input  a3,
  input  sign_a,
  input  b0,
  input  b1,
  input  b2,
  input  b3,
  input  sign_b,
  output out_12,
  output out_13,
  output out_14,
  output out_15,
  output out_16,
  output out_17,
  output out_18,
  output out_19,
  output Zero_Flag,
  output Sign
);

  wire check_result_1_out_7, check_result_1_out_8, check_result_1_out_9, check_result_1_out_10,
       check_result_1_out_11, check_sign_complement_1_complement_checker, fulladder_1_out_4,
       fulladder_1_out_5, fulladder_2_out_4, fulladder_2_out_5, fulladder_3_out_4, fulladder_3_out_5,
       fulladder_4_out_4, fulladder_4_out_5, fulladder_5_out_4, fulladder_5_out_5, xor_1_out, xor_2_out,
       xor_3_out, xor_4_out, xor_5_out;

  xor xor_1 (xor_1_out, Mode, sign_b);
  Check_result check_result_1 (
    .\checker (sign_a), .c0(a0), .c1(a1), .c2(a2), .c3(a3), .c4(1'b0), .out_7(check_result_1_out_7),
    .out_8(check_result_1_out_8), .out_9(check_result_1_out_9), .out_10(check_result_1_out_10),
    .out_11(check_result_1_out_11));
  xor xor_2 (xor_2_out, xor_1_out, b0);
  xor xor_3 (xor_3_out, xor_1_out, b1);
  xor xor_4 (xor_4_out, xor_1_out, b2);
  xor xor_5 (xor_5_out, xor_1_out, b3);
  FullAdder fulladder_1 (
    .in_1(xor_1_out), .in_2(check_result_1_out_7), .in_3(xor_2_out), .out_4(fulladder_1_out_4),
    .out_5(fulladder_1_out_5));
  FullAdder fulladder_2 (
    .in_1(fulladder_1_out_5), .in_2(check_result_1_out_8), .in_3(xor_3_out), .out_4(fulladder_2_out_4),
    .out_5(fulladder_2_out_5));
  FullAdder fulladder_3 (
    .in_1(fulladder_2_out_5), .in_2(check_result_1_out_9), .in_3(xor_4_out), .out_4(fulladder_3_out_4),
    .out_5(fulladder_3_out_5));
  FullAdder fulladder_4 (
    .in_1(fulladder_3_out_5), .in_2(check_result_1_out_10), .in_3(xor_5_out), .out_4(fulladder_4_out_4),
    .out_5(fulladder_4_out_5));
  FullAdder fulladder_5 (
    .in_1(fulladder_4_out_5), .in_2(sign_a), .in_3(xor_1_out), .out_4(fulladder_5_out_4),
    .out_5(fulladder_5_out_5));
  Check_Sign__complement check_sign_complement_1 (
    .Sign_a(sign_a), .Sign_B___Operation(xor_1_out), .Final_Carry(fulladder_5_out_5), .Sign(Sign),
    .Complement_checker(check_sign_complement_1_complement_checker));
  Check_result check_result_2 (
    .\checker (check_sign_complement_1_complement_checker), .c0(fulladder_1_out_4), .c1(fulladder_2_out_4),
    .c2(fulladder_3_out_4), .c3(fulladder_4_out_4), .c4(fulladder_5_out_4), .out_7(out_12), .out_8(out_13),
    .out_9(out_14), .out_10(out_15), .out_11(out_16));
  Zero_Flag_Addition zero_flag_addition_1 (
    .in_1(out_16), .in_2(out_15), .in_3(out_14), .in_4(out_13), .in_5(out_12), .Zero_Flag(Zero_Flag));

  assign out_17 = 1'b0;
  assign out_18 = 1'b0;
  assign out_19 = 1'b0;

  // Notes on the sheet:
  //   Check Sign & Complement
  //   Result
endmodule

module Check_Sign__complement (
  input  Sign_a,
  input  Sign_B___Operation,
  input  Final_Carry,
  output Sign,
  output Complement_checker
);

  wire and_1_out, and_2_out, and_3_out, not_1_out, or_1_out, xor_1_out;

  not not_1 (not_1_out, Final_Carry);
  and and_1 (and_1_out, Sign_a, not_1_out);
  and and_2 (and_2_out, Sign_a, Sign_B___Operation);
  and and_3 (and_3_out, Sign_B___Operation, not_1_out);
  xor xor_1 (xor_1_out, Sign_a, Sign_B___Operation);
  or or_1 (or_1_out, and_1_out, and_2_out);
  xor xor_2 (Sign, Final_Carry, xor_1_out);
  or or_2 (Complement_checker, or_1_out, and_3_out);

  // Notes on the sheet:
  //   b4 XOR Sign
endmodule

module Check_result (
  input  \checker ,
  input  c0,
  input  c1,
  input  c2,
  input  c3,
  input  c4,
  output out_7,
  output out_8,
  output out_9,
  output out_10,
  output out_11
);

  wire and_1_out, and_2_out, and_3_out, and_4_out, and_5_out, and_6_out, and_7_out, and_8_out, not_1_out,
       or_1_out, or_2_out, or_3_out, or_4_out, or_5_out, or_6_out, xor_1_out, xor_2_out, xor_3_out, xor_4_out;

  not not_1 (not_1_out, \checker );
  or or_1 (or_1_out, c0, c1);
  or or_2 (or_2_out, c0, c1);
  xor xor_1 (xor_1_out, c0, c1);
  or or_3 (or_3_out, c0, c1);
  or or_4 (or_4_out, or_2_out, c2);
  xor xor_2 (xor_2_out, or_1_out, c2);
  or or_5 (or_5_out, or_3_out, c2);
  or or_6 (or_6_out, or_4_out, c3);
  xor xor_3 (xor_3_out, or_5_out, c3);
  xor xor_4 (xor_4_out, or_6_out, c4);
  and and_1 (and_1_out, not_1_out, c1);
  and and_2 (and_2_out, xor_1_out, \checker );
  and and_3 (and_3_out, \checker , xor_2_out);
  and and_4 (and_4_out, not_1_out, c2);
  and and_5 (and_5_out, \checker , xor_3_out);
  and and_6 (and_6_out, not_1_out, c3);
  and and_7 (and_7_out, \checker , xor_4_out);
  and and_8 (and_8_out, c4, not_1_out);
  or or_7 (out_8, and_1_out, and_2_out);
  or or_8 (out_9, and_3_out, and_4_out);
  or or_9 (out_10, and_5_out, and_6_out);
  or or_10 (out_11, and_7_out, and_8_out);

  assign out_7 = c0;
endmodule

module Zero_Flag_Addition (
  input  in_1,
  input  in_2,
  input  in_3,
  input  in_4,
  input  in_5,
  output Zero_Flag
);

  wire or_1_out, or_2_out, or_3_out, or_4_out;

  or or_1 (or_1_out, in_1, in_2);
  or or_2 (or_2_out, or_1_out, in_3);
  or or_3 (or_3_out, or_2_out, in_4);
  or or_4 (or_4_out, or_3_out, in_5);
  not not_1 (Zero_Flag, or_4_out);
endmodule
