// Logisim project BCD to seven segment code.circ as structural Verilog
module BCD_to_7segment (
  input  A,
  input  in_2,
  input  C,
  input  D,
  output out_5,
  output out_6,
  output out_7,
  output out_8,
  output out_9,
  output out_10,
  output out_11
);

  wire and_1_out, and_2_out, and_3_out, and_4_out, and_5_out, and_6_out, and_7_out, and_8_out, and_9_out,
       not_1_out, not_2_out, not_3_out, or_2_out, or_3_out, or_4_out, or_5_out, or_6_out, or_7_out, or_9_out,
       or_11_out, or_12_out, or_13_out, or_16_out;

  not not_1 (not_1_out, in_2);
  not not_2 (not_2_out, C);
  not not_3 (not_3_out, D);
  and and_1 (and_1_out, not_1_out, not_3_out);
  and and_2 (and_2_out, in_2, D);
  and and_3 (and_3_out, not_2_out, not_3_out);
  and and_4 (and_4_out, not_3_out, C);
  and and_5 (and_5_out, not_1_out, C);
  and and_6 (and_6_out, not_2_out, in_2);
  and and_7 (and_7_out, C, D);
  and and_8 (and_8_out, in_2, not_3_out);
  and and_9 (and_9_out, and_6_out, D);
  or or_1 (out_9, and_4_out, and_1_out);
  or or_2 (or_2_out, A, and_6_out);
  or or_3 (or_3_out, A, and_6_out);
  or or_4 (or_4_out, A, and_1_out);
  or or_5 (or_5_out, and_7_out, not_1_out);
  or or_6 (or_6_out, A, and_1_out);
  or or_7 (or_7_out, or_2_out, and_8_out);
  or or_8 (out_10, or_7_out, and_3_out);
  or or_9 (or_9_out, or_3_out, and_5_out);
  or or_10 (out_11, or_9_out, and_4_out);
  or or_11 (or_11_out, or_4_out, and_2_out);
  or or_12 (or_12_out, in_2, D);
  or or_13 (or_13_out, or_6_out, and_4_out);
  or or_14 (out_6, or_5_out, and_3_out);
  or or_15 (out_7, or_12_out, not_2_out);
  or or_16 (or_16_out, or_13_out, and_5_out);
  or or_17 (out_5, or_11_out, C);
  or or_18 (out_8, or_16_out, and_9_out);

  // Notes on the sheet:
  //   B
  //   d-c
  //   CB-
  //   B-D-
  //   BD
  //   CD
  //   C-D-
  //   C-B
  //   C-BD
endmodule

module half_adder (
  input  in_1,
  input  in_2,
  output out_3,
  output out_4
);

  xor xor_1 (out_3, in_1, in_2);
  and and_1 (out_4, in_1, in_2);
endmodule

module full_adder (
  input  in_1,
  input  in_2,
  input  in_3,
  output out_4,
  output out_5
);

  wire half_adder_1_out_3, half_adder_1_out_4, half_adder_2_out_4;

  half_adder half_adder_1 (.in_1(in_1), .in_2(in_2), .out_3(half_adder_1_out_3), .out_4(half_adder_1_out_4));
  half_adder half_adder_2 (.in_1(half_adder_1_out_3), .in_2(in_3), .out_3(out_4), .out_4(half_adder_2_out_4));
  or or_1 (out_5, half_adder_2_out_4, half_adder_1_out_4);
endmodule

module subtraction (
  input  in_1,
  input  in_2,
  input  in_3,
  input  in_4,
  input  in_5,
  input  in_6,
  input  in_7,
  input  in_8,
  input  in_9,
  output out_10,
  output out_11,
  output out_12,
  output out_13,
  output out_14
);

  wire full_adder_1_out_5, full_adder_2_out_5, full_adder_3_out_5, not_1_out, not_2_out, not_3_out, not_4_out;

  not not_1 (not_1_out, in_2);
  not not_2 (not_2_out, in_6);
  not not_3 (not_3_out, in_8);
  not not_4 (not_4_out, in_4);
  full_adder full_adder_1 (.in_1(in_1), .in_2(not_1_out), .in_3(in_3), .out_4(out_10), .out_5(full_adder_1_out_5));
  full_adder full_adder_2 (
    .in_1(full_adder_1_out_5), .in_2(not_4_out), .in_3(in_5), .out_4(out_11), .out_5(full_adder_2_out_5));
  full_adder full_adder_3 (
    .in_1(full_adder_2_out_5), .in_2(not_2_out), .in_3(in_7), .out_4(out_12), .out_5(full_adder_3_out_5));
  full_adder full_adder_4 (.in_1(full_adder_3_out_5), .in_2(not_3_out), .in_3(in_9), .out_4(out_13), .out_5(out_14));
endmodule

module INTEGER_DIVISION (
  input  A_sign,
  input  b4,
  input  b1,
  input  b2,
  input  b3,
  input  a0,
  input  a1,
  input  a2,
  input  a3,
  input  b0,
  output d0,
  output d1,
  output d2,
  output d3,
  output out_15,
  output out_16,
  output out_17,
  output out_18,
  output sign,
  output zero_divider,
  output zero_input
);

  wire comparitor_1_out_10, comparitor_1_out_11, comparitor_2_out_10, comparitor_2_out_11,
       comparitor_3_out_10, comparitor_3_out_11, comparitor_4_out_10, comparitor_4_out_11,
       multiplayer4_1_1_out_6, multiplayer4_1_1_out_7, multiplayer4_1_1_out_8, multiplayer4_1_1_out_9,
       multiplayer4_1_2_out_6, multiplayer4_1_2_out_7, multiplayer4_1_2_out_8, multiplayer4_1_2_out_9,
       multiplayer4_1_3_out_6, multiplayer4_1_3_out_7, multiplayer4_1_3_out_8, multiplayer4_1_3_out_9,
       or_1_out, or_2_out, or_3_out, or_4_out, or_5_out, or_7_out, subtraction_1_out_10,
       subtraction_1_out_11, subtraction_1_out_12, subtraction_2_out_10, subtraction_2_out_11,
       subtraction_2_out_12, subtraction_3_out_10, subtraction_3_out_11, subtraction_3_out_12;

  or or_1 (or_1_out, b0, b1);
  or or_2 (or_2_out, a3, a2);
  or or_3 (or_3_out, or_2_out, a1);
  COMPARITOR comparitor_1 (
    .in_1(b3), .in_2(b2), .in_3(b1), .in_4(b0), .in_5(1'b0), .in_6(1'b0), .in_7(1'b0), .in_8(a3),
    .out_10(comparitor_1_out_10), .out_11(comparitor_1_out_11));  // open: out_9
  or or_4 (or_4_out, or_1_out, b2);
  or or_5 (or_5_out, or_3_out, a0);
  or or_6 (d3, comparitor_1_out_10, comparitor_1_out_11);
  or or_7 (or_7_out, or_4_out, b3);
  not not_1 (zero_divider, or_7_out);
  MULTIPLAYER4_1 multiplayer4_1_1 (
    .in_1(b0), .in_2(b1), .in_3(b2), .in_4(b3), .in_5(d3), .out_6(multiplayer4_1_1_out_6),
    .out_7(multiplayer4_1_1_out_7), .out_8(multiplayer4_1_1_out_8), .out_9(multiplayer4_1_1_out_9));
  xor xor_1 (sign, b4, A_sign);
  not not_2 (zero_input, or_5_out);
  subtraction subtraction_1 (
    .in_1(1'b1), .in_2(multiplayer4_1_1_out_6), .in_3(a3), .in_4(multiplayer4_1_1_out_7), .in_5(1'b0),
    .in_6(multiplayer4_1_1_out_8), .in_7(1'b0), .in_8(multiplayer4_1_1_out_9), .in_9(1'b0),
    .out_10(subtraction_1_out_10), .out_11(subtraction_1_out_11), .out_12(subtraction_1_out_12));  // open: out_13, out_14
  COMPARITOR comparitor_2 (
    .in_1(b3), .in_2(b2), .in_3(b1), .in_4(b0), .in_5(subtraction_1_out_12), .in_6(subtraction_1_out_11),
    .in_7(subtraction_1_out_10), .in_8(a2), .out_10(comparitor_2_out_10), .out_11(comparitor_2_out_11));  // open: out_9
  or or_8 (d2, comparitor_2_out_10, comparitor_2_out_11);
  MULTIPLAYER4_1 multiplayer4_1_2 (
    .in_1(b0), .in_2(b1), .in_3(b2), .in_4(b3), .in_5(d2), .out_6(multiplayer4_1_2_out_6),
    .out_7(multiplayer4_1_2_out_7), .out_8(multiplayer4_1_2_out_8), .out_9(multiplayer4_1_2_out_9));
  subtraction subtraction_2 (
    .in_1(1'b1), .in_2(multiplayer4_1_2_out_6), .in_3(a2), .in_4(multiplayer4_1_2_out_7),
    .in_5(subtraction_1_out_10), .in_6(multiplayer4_1_2_out_8), .in_7(subtraction_1_out_11),
    .in_8(multiplayer4_1_2_out_9), .in_9(subtraction_1_out_12), .out_10(subtraction_2_out_10),
    .out_11(subtraction_2_out_11), .out_12(subtraction_2_out_12));  // open: out_13, out_14
  COMPARITOR comparitor_3 (
    .in_1(b3), .in_2(b2), .in_3(b1), .in_4(b0), .in_5(subtraction_2_out_12), .in_6(subtraction_2_out_11),
    .in_7(subtraction_2_out_10), .in_8(a1), .out_10(comparitor_3_out_10), .out_11(comparitor_3_out_11));  // open: out_9
  MULTIPLAYER4_1 multiplayer4_1_3 (
    .in_1(b0), .in_2(b1), .in_3(b2), .in_4(b3), .in_5(d1), .out_6(multiplayer4_1_3_out_6),
    .out_7(multiplayer4_1_3_out_7), .out_8(multiplayer4_1_3_out_8), .out_9(multiplayer4_1_3_out_9));
  or or_9 (d1, comparitor_3_out_10, comparitor_3_out_11);
  subtraction subtraction_3 (
    .in_1(1'b1), .in_2(multiplayer4_1_3_out_6), .in_3(a1), .in_4(multiplayer4_1_3_out_7),
    .in_5(subtraction_2_out_10), .in_6(multiplayer4_1_3_out_8), .in_7(subtraction_2_out_11),
    .in_8(multiplayer4_1_3_out_9), .in_9(subtraction_2_out_12), .out_10(subtraction_3_out_10),
    .out_11(subtraction_3_out_11), .out_12(subtraction_3_out_12));  // open: out_13, out_14
  COMPARITOR comparitor_4 (
    .in_1(b3), .in_2(b2), .in_3(b1), .in_4(b0), .in_5(subtraction_3_out_12), .in_6(subtraction_3_out_11),
    .in_7(subtraction_3_out_10), .in_8(a0), .out_10(comparitor_4_out_10), .out_11(comparitor_4_out_11));  // open: out_9
  or or_10 (d0, comparitor_4_out_10, comparitor_4_out_11);

  assign out_15 = 1'b0;
  assign out_16 = 1'b0;
  assign out_17 = 1'b0;
  assign out_18 = 1'b0;

  // Notes on the sheet:
  //   A0
  //   A1
  //   A2
  //   A3
  //   A4
  //   B0
  //   B1
  //   B2
  //   B3
  //   B4
  //   zero flag
  //   SIGNE
  //   zero input
endmodule

module MULTIPLAYER4_1 (
  input  in_1,
  input  in_2,
  input  in_3,
  input  in_4,
  input  in_5,
  output out_6,
  output out_7,
  output out_8,
  output out_9
);

  and and_1 (out_6, in_1, in_5);
  and and_2 (out_7, in_2, in_5);
  and and_3 (out_8, in_3, in_5);
  and and_4 (out_9, in_4, in_5);
endmodule

module COMPARITOR (
  input  in_1,
  input  in_2,
  input  in_3,
  input  in_4,
  input  in_5,
  input  in_6,
  input  in_7,
  input  in_8,
  output out_9,
  output out_10,
  output out_11
);

  wire and_1_out, and_2_out, and_3_out, and_4_out, and_5_out, and_6_out, and_7_out, and_8_out, and_9_out,
       and_10_out, and_11_out, and_12_out, and_13_out, and_14_out, and_15_out, and_16_out, and_17_out,
       and_18_out, and_19_out, and_20_out, and_22_out, and_23_out, nor_1_out, nor_2_out, nor_3_out,
       nor_4_out, not_1_out, not_2_out, not_3_out, not_4_out, not_5_out, not_6_out, not_7_out, not_8_out,
       or_1_out, or_2_out, or_3_out, or_4_out;

  not not_1 (not_1_out, in_5);
  not not_2 (not_2_out, in_1);
  not not_3 (not_3_out, in_6);
  not not_4 (not_4_out, in_2);
  not not_5 (not_5_out, in_7);
  not not_6 (not_6_out, in_3);
  not not_7 (not_7_out, in_8);
  not not_8 (not_8_out, in_4);
  and and_1 (and_1_out, in_1, not_1_out);
  and and_2 (and_2_out, not_2_out, in_5);
  and and_3 (and_3_out, in_2, not_3_out);
  and and_4 (and_4_out, not_4_out, in_6);
  and and_5 (and_5_out, in_3, not_5_out);
  and and_6 (and_6_out, not_6_out, in_7);
  and and_7 (and_7_out, in_4, not_7_out);
  and and_8 (and_8_out, not_8_out, in_8);
  nor nor_1 (nor_1_out, and_1_out, and_2_out);
  nor nor_2 (nor_2_out, and_3_out, and_4_out);
  nor nor_3 (nor_3_out, and_5_out, and_6_out);
  nor nor_4 (nor_4_out, and_7_out, and_8_out);
  and and_9 (and_9_out, nor_1_out, and_3_out);
  and and_10 (and_10_out, nor_1_out, and_4_out);
  and and_11 (and_11_out, nor_1_out, nor_2_out);
  and and_12 (and_12_out, nor_1_out, nor_2_out);
  and and_13 (and_13_out, nor_1_out, nor_2_out);
  and and_14 (and_14_out, nor_1_out, nor_2_out);
  and and_15 (and_15_out, nor_1_out, nor_2_out);
  and and_16 (and_16_out, nor_3_out, nor_4_out);
  and and_17 (and_17_out, and_5_out, and_11_out);
  and and_18 (and_18_out, and_12_out, and_6_out);
  and and_19 (and_19_out, nor_3_out, and_13_out);
  and and_20 (and_20_out, and_14_out, nor_3_out);
  and and_21 (out_11, and_15_out, and_16_out);
  and and_22 (and_22_out, and_7_out, and_19_out);
  and and_23 (and_23_out, and_20_out, and_8_out);
  or or_1 (or_1_out, and_2_out, and_10_out);
  or or_2 (or_2_out, and_1_out, and_9_out);
  or or_3 (or_3_out, or_1_out, and_18_out);
  or or_4 (or_4_out, or_2_out, and_17_out);
  or or_5 (out_10, or_3_out, and_23_out);
  or or_6 (out_9, or_4_out, and_22_out);
endmodule
