// Logisim project Mltiplier and from binary to BCD .circ as structural Verilog
module Half_Adder (
  input  x,
  input  y,
  output sum,
  output carry
);

  xor xor_1 (sum, x, y);
  and and_1 (carry, y, x);
endmodule

module Full_Adder (
  input  x,
  input  y,
  input  carry,
  output sum,
  output carry_2
);

  wire half_adder_1_carry, half_adder_1_sum, half_adder_2_carry;

  Half_Adder half_adder_1 (.x(x), .y(y), .sum(half_adder_1_sum), .carry(half_adder_1_carry));
  Half_Adder half_adder_2 (.x(half_adder_1_sum), .y(carry), .sum(sum), .carry(half_adder_2_carry));
  or or_1 (carry_2, half_adder_2_carry, half_adder_1_carry);

  // Notes on the sheet:
  //   Half Adder
endmodule

module shifter (
  input  a0,
  input  a1,
  input  a2,
  input  a3,
  output out_5,
  output out_6,
  output out_7,
  output out_8
);

  wire and_1_out, and_2_out, and_3_out, and_4_out, and_5_out, and_6_out, and_7_out, and_8_out, and_9_out,
       and_10_out, and_11_out, and_12_out, and_13_out, and_14_out, and_15_out, and_16_out, and_17_out,
       and_18_out, not_1_out, not_2_out, not_3_out, not_4_out, not_5_out, not_6_out, not_7_out, not_8_out,
       or_1_out, or_4_out, or_6_out;

  or or_1 (or_1_out, a0, a1);
  and and_1 (and_1_out, or_1_out, a2);
  and and_2 (and_2_out, not_5_out, a3);
  or or_2 (out_5, and_1_out, and_3_out);
  and and_3 (and_3_out, and_2_out, not_3_out);
  and and_4 (and_4_out, a2, not_1_out);
  not not_1 (not_1_out, a1);
  not not_2 (not_2_out, a0);
  and and_5 (and_5_out, and_4_out, not_2_out);
  and and_6 (and_6_out, a3, a0);
  or or_3 (out_6, and_5_out, and_6_out);
  not not_3 (not_3_out, a1);
  and and_7 (and_7_out, a3, not_3_out);
  not not_4 (not_4_out, a0);
  and and_8 (and_8_out, and_7_out, not_4_out);
  not not_5 (not_5_out, a2);
  and and_9 (and_9_out, a1, not_5_out);
  and and_10 (and_10_out, and_9_out, not_8_out);
  or or_4 (or_4_out, and_8_out, and_10_out);
  or or_5 (out_7, or_4_out, and_12_out);
  and and_11 (and_11_out, a0, not_8_out);
  and and_12 (and_12_out, and_11_out, a1);
  not not_6 (not_6_out, a1);
  and and_13 (and_13_out, a1, a2);
  and and_14 (and_14_out, and_13_out, not_7_out);
  not not_7 (not_7_out, a0);
  and and_15 (and_15_out, a3, not_7_out);
  or or_6 (or_6_out, and_14_out, and_16_out);
  not not_8 (not_8_out, a3);
  and and_16 (and_16_out, and_15_out, not_6_out);
  or or_7 (out_8, or_6_out, and_18_out);
  and and_17 (and_17_out, not_8_out, not_5_out);
  and and_18 (and_18_out, and_17_out, a0);
endmodule

module Binary_to_BCD (
  input  in_1,
  input  in_2,
  input  in_3,
  input  in_4,
  input  in_5,
  input  in_6,
  input  in_7,
  input  in_8,
  output out_9,
  output out_10,
  output out_11,
  output out_12,
  output out_13,
  output out_14,
  output out_15,
  output out_16,
  output out_17,
  output out_18,
  output out_19,
  output out_20
);

  wire c1_out_5, c1_out_6, c1_out_7, c1_out_8, c2_out_5, c2_out_6, c2_out_7, c2_out_8, c3_out_5, c3_out_6,
       c3_out_7, c3_out_8, c4_out_5, c4_out_6, c4_out_7, c4_out_8, c6_out_6, c6_out_7, c6_out_8;

  shifter c1 (
    .a0(in_3), .a1(in_2), .a2(in_1), .a3(1'b0), .out_5(c1_out_5), .out_6(c1_out_6), .out_7(c1_out_7),
    .out_8(c1_out_8));
  shifter c2 (
    .a0(in_4), .a1(c1_out_8), .a2(c1_out_7), .a3(c1_out_6), .out_5(c2_out_5), .out_6(c2_out_6),
    .out_7(c2_out_7), .out_8(c2_out_8));
  shifter c6 (
    .a0(c3_out_5), .a1(c2_out_5), .a2(c1_out_5), .a3(1'b0), .out_5(out_11), .out_6(c6_out_6),
    .out_7(c6_out_7), .out_8(c6_out_8));
  shifter c3 (
    .a0(in_5), .a1(c2_out_8), .a2(c2_out_7), .a3(c2_out_6), .out_5(c3_out_5), .out_6(c3_out_6),
    .out_7(c3_out_7), .out_8(c3_out_8));
  shifter c7 (
    .a0(c4_out_5), .a1(c6_out_8), .a2(c6_out_7), .a3(c6_out_6), .out_5(out_12), .out_6(out_13),
    .out_7(out_14), .out_8(out_15));
  shifter c4 (
    .a0(in_6), .a1(c3_out_8), .a2(c3_out_7), .a3(c3_out_6), .out_5(c4_out_5), .out_6(c4_out_6),
    .out_7(c4_out_7), .out_8(c4_out_8));
  shifter c5 (
    .a0(in_7), .a1(c4_out_8), .a2(c4_out_7), .a3(c4_out_6), .out_5(out_16), .out_6(out_17), .out_7(out_18),
    .out_8(out_19));

  assign out_9 = 1'b0;
  assign out_10 = 1'b0;
  assign out_20 = in_8;
endmodule

module multiplicator (
  input  a0,
  input  a1,
  input  a2,
  input  a3,
  input  sign_1,
  input  b0,
  input  b1,
  input  b2,
  input  b3,
  input  sign_2,
  output c1,
  output c0,
  output c2,
  output sign,
  output c3,
  output c7,
  output c6,
  output c5,
  output c4
);

  wire and_1_out, and_2_out, and_3_out, and_4_out, and_5_out, and_6_out, and_7_out, and_8_out, and_9_out,
       and_10_out, and_11_out, and_12_out, and_13_out, and_14_out, and_15_out, full_adder_2_carry_2,
       full_adder_3_carry_2, full_adder_3_sum, full_adder_4_carry_2, full_adder_4_sum, full_adder_5_carry_2,
       full_adder_5_sum, full_adder_6_carry_2, full_adder_7_carry_2, full_adder_7_sum, full_adder_8_carry_2,
       full_adder_8_sum, half_adder_1_carry, half_adder_2_carry, half_adder_2_sum, half_adder_3_carry,
       half_adder_4_carry;

  xor xor_1 (sign, sign_2, sign_1);
  and and_1 (and_1_out, b3, a3);
  Full_Adder full_adder_1 (
    .x(full_adder_2_carry_2), .y(and_1_out), .carry(full_adder_3_carry_2), .sum(c6), .carry_2(c7));
  and and_2 (and_2_out, b3, a2);
  and and_3 (and_3_out, b2, a3);
  Full_Adder full_adder_2 (
    .x(and_3_out), .y(and_2_out), .carry(full_adder_3_sum), .sum(c5), .carry_2(full_adder_2_carry_2));
  and and_4 (and_4_out, b3, a1);
  Full_Adder full_adder_3 (
    .x(half_adder_1_carry), .y(full_adder_4_carry_2), .carry(full_adder_5_carry_2), .sum(full_adder_3_sum),
    .carry_2(full_adder_3_carry_2));
  Half_Adder half_adder_1 (.x(full_adder_4_sum), .y(and_4_out), .sum(c4), .carry(half_adder_1_carry));
  and and_5 (and_5_out, b2, a2);
  and and_6 (and_6_out, b1, a3);
  Full_Adder full_adder_4 (
    .x(and_6_out), .y(and_5_out), .carry(full_adder_5_sum), .sum(full_adder_4_sum),
    .carry_2(full_adder_4_carry_2));
  and and_7 (and_7_out, b3, a0);
  and and_8 (and_8_out, b2, a1);
  Full_Adder full_adder_5 (
    .x(full_adder_6_carry_2), .y(full_adder_7_carry_2), .carry(half_adder_2_carry), .sum(full_adder_5_sum),
    .carry_2(full_adder_5_carry_2));
  and and_9 (and_9_out, a2, b1);
  Full_Adder full_adder_6 (
    .x(full_adder_7_sum), .y(and_8_out), .carry(and_7_out), .sum(c3), .carry_2(full_adder_6_carry_2));
  and and_10 (and_10_out, b0, a3);
  Full_Adder full_adder_7 (
    .x(and_10_out), .y(and_9_out), .carry(half_adder_2_sum), .sum(full_adder_7_sum),
    .carry_2(full_adder_7_carry_2));
  and and_11 (and_11_out, b2, a0);
  Half_Adder half_adder_2 (
    .x(half_adder_3_carry), .y(full_adder_8_carry_2), .sum(half_adder_2_sum), .carry(half_adder_2_carry));
  Half_Adder half_adder_3 (.x(full_adder_8_sum), .y(and_11_out), .sum(c2), .carry(half_adder_3_carry));
  and and_12 (and_12_out, b1, a1);
  Full_Adder full_adder_8 (
    .x(and_13_out), .y(and_12_out), .carry(half_adder_4_carry), .sum(full_adder_8_sum),
    .carry_2(full_adder_8_carry_2));
  and and_13 (and_13_out, b0, a2);
  and and_14 (and_14_out, b1, a0);
  Half_Adder half_adder_4 (.x(and_15_out), .y(and_14_out), .sum(c1), .carry(half_adder_4_carry));
  and and_15 (and_15_out, b0, a1);
  and and_16 (c0, b0, a0);
endmodule

module multiplicator_with_flag_zero (
  input  a0,
  input  a1,
  input  a2,
  input  a3,
  input  sigb_1,
  input  b0,
  input  b1,
  input  b2,
  input  b3,
  input  sign_2,
  output _8,
  output _7,
  output _6,
  output _5,
  output _4,
  output _3,
  output _2,
  output _1,
  output sign_flag,
  output zero_flag
);

  wire multiplicator_1_sign, not_2_out, or_1_out, or_2_out, or_3_out, or_4_out, or_5_out, or_6_out, or_7_out;

  or or_1 (or_1_out, _6, _5);
  or or_2 (or_2_out, or_3_out, or_1_out);
  or or_3 (or_3_out, _8, _7);
  or or_4 (or_4_out, _4, _3);
  or or_5 (or_5_out, _2, _1);
  or or_6 (or_6_out, or_4_out, or_5_out);
  or or_7 (or_7_out, or_2_out, or_6_out);
  not not_1 (zero_flag, or_7_out);
  not not_2 (not_2_out, zero_flag);
  and and_1 (sign_flag, not_2_out, multiplicator_1_sign);
  multiplicator multiplicator_1 (
    .a0(a0), .a1(a1), .a2(a2), .a3(a3), .sign_1(sigb_1), .b0(b0), .b1(b1), .b2(b2), .b3(b3), .sign_2(sign_2),
    .sign(multiplicator_1_sign), .c7(_8), .c6(_7), .c5(_6), .c4(_5), .c3(_4), .c2(_3), .c1(_2), .c0(_1));
endmodule
