// Logisim project Project Logic Design.circ as structural Verilog
module Logic_Design_project (
  input  in_1,
  input  in_2,
  input  a0,
  input  a1,
  input  a2,
  input  a3,
  input  a_sign,
  input  b0,
  input  b1,
  input  b2,
  input  b3,
  input  b_sign,
  output sign,
  output Zero_Divider,
  output Zero_Flag
);

  wire alu_1_out_13, alu_1_out_14, alu_1_out_15, alu_1_out_16, alu_1_out_17, alu_1_out_18, alu_1_out_19,
       alu_1_out_20, bcd_to_7segment_1_out_5, bcd_to_7segment_1_out_6, bcd_to_7segment_1_out_7,
       bcd_to_7segment_1_out_8, bcd_to_7segment_1_out_9, bcd_to_7segment_1_out_10, bcd_to_7segment_1_out_11,
       bcd_to_7segment_2_out_5, bcd_to_7segment_2_out_6, bcd_to_7segment_2_out_7, bcd_to_7segment_2_out_8,
       bcd_to_7segment_2_out_9, bcd_to_7segment_2_out_10, bcd_to_7segment_2_out_11, bcd_to_7segment_3_out_5,
       bcd_to_7segment_3_out_6, bcd_to_7segment_3_out_7, bcd_to_7segment_3_out_8, bcd_to_7segment_3_out_9,
       bcd_to_7segment_3_out_10, bcd_to_7segment_3_out_11, binary_to_bcd_1_out_9, binary_to_bcd_1_out_10,
       binary_to_bcd_1_out_11, binary_to_bcd_1_out_12, binary_to_bcd_1_out_13, binary_to_bcd_1_out_14,
       binary_to_bcd_1_out_15, binary_to_bcd_1_out_16, binary_to_bcd_1_out_17, binary_to_bcd_1_out_18,
       binary_to_bcd_1_out_19, binary_to_bcd_1_out_20;

  ALU alu_1 (
    .a0(a0), .a1(a1), .a2(a2), .a3(a3), .sign_a(a_sign), .b0(b0), .b1(b1), .b2(b2), .b3(b3), .sign_b(b_sign),
    .in_1(in_1), .in_2(in_2), .out_21(Zero_Flag), .Zero_Divider(Zero_Divider), .Sign_Flag(sign),
    .out_13(alu_1_out_13), .out_14(alu_1_out_14), .out_15(alu_1_out_15), .out_16(alu_1_out_16),
    .out_17(alu_1_out_17), .out_18(alu_1_out_18), .out_19(alu_1_out_19), .out_20(alu_1_out_20));
  Binary_to_BCD binary_to_bcd_1 (
    .in_1(alu_1_out_20), .in_2(alu_1_out_19), .in_3(alu_1_out_18), .in_4(alu_1_out_17), .in_5(alu_1_out_16),
    .in_6(alu_1_out_15), .in_7(alu_1_out_14), .in_8(alu_1_out_13), .out_9(binary_to_bcd_1_out_9),
    .out_10(binary_to_bcd_1_out_10), .out_11(binary_to_bcd_1_out_11), .out_12(binary_to_bcd_1_out_12),
    .out_13(binary_to_bcd_1_out_13), .out_14(binary_to_bcd_1_out_14), .out_15(binary_to_bcd_1_out_15),
    .out_16(binary_to_bcd_1_out_16), .out_17(binary_to_bcd_1_out_17), .out_18(binary_to_bcd_1_out_18),
    .out_19(binary_to_bcd_1_out_19), .out_20(binary_to_bcd_1_out_20));
  BCD_to_7segment bcd_to_7segment_1 (
    .A(binary_to_bcd_1_out_17), .in_2(binary_to_bcd_1_out_18), .C(binary_to_bcd_1_out_19),
    .D(binary_to_bcd_1_out_20), .out_5(bcd_to_7segment_1_out_5), .out_6(bcd_to_7segment_1_out_6),
    .out_7(bcd_to_7segment_1_out_7), .out_8(bcd_to_7segment_1_out_8), .out_9(bcd_to_7segment_1_out_9),
    .out_10(bcd_to_7segment_1_out_10), .out_11(bcd_to_7segment_1_out_11));
  BCD_to_7segment bcd_to_7segment_2 (
    .A(binary_to_bcd_1_out_13), .in_2(binary_to_bcd_1_out_14), .C(binary_to_bcd_1_out_15),
    .D(binary_to_bcd_1_out_16), .out_5(bcd_to_7segment_2_out_5), .out_6(bcd_to_7segment_2_out_6),
    .out_7(bcd_to_7segment_2_out_7), .out_8(bcd_to_7segment_2_out_8), .out_9(bcd_to_7segment_2_out_9),
    .out_10(bcd_to_7segment_2_out_10), .out_11(bcd_to_7segment_2_out_11));
  BCD_to_7segment bcd_to_7segment_3 (
    .A(binary_to_bcd_1_out_9), .in_2(binary_to_bcd_1_out_10), .C(binary_to_bcd_1_out_11),
    .D(binary_to_bcd_1_out_12), .out_5(bcd_to_7segment_3_out_5), .out_6(bcd_to_7segment_3_out_6),
    .out_7(bcd_to_7segment_3_out_7), .out_8(bcd_to_7segment_3_out_8), .out_9(bcd_to_7segment_3_out_9),
    .out_10(bcd_to_7segment_3_out_10), .out_11(bcd_to_7segment_3_out_11));
  _7_Segment_Display u_7_segment_display_1 (
    .g(bcd_to_7segment_3_out_11), .f(bcd_to_7segment_3_out_10), .a(bcd_to_7segment_3_out_5),
    .b(bcd_to_7segment_3_out_6), .e(bcd_to_7segment_3_out_9), .d(bcd_to_7segment_3_out_8),
    .c(bcd_to_7segment_3_out_7));  // open: dp
  _7_Segment_Display u_7_segment_display_2 (
    .g(bcd_to_7segment_1_out_11), .f(bcd_to_7segment_1_out_10), .a(bcd_to_7segment_1_out_5),
    .b(bcd_to_7segment_1_out_6), .e(bcd_to_7segment_1_out_9), .d(bcd_to_7segment_1_out_8),
    .c(bcd_to_7segment_1_out_7));  // open: dp
  _7_Segment_Display u_7_segment_display_3 (
    .g(bcd_to_7segment_2_out_11), .f(bcd_to_7segment_2_out_10), .a(bcd_to_7segment_2_out_5),
    .b(bcd_to_7segment_2_out_6), .e(bcd_to_7segment_2_out_9), .d(bcd_to_7segment_2_out_8),
    .c(bcd_to_7segment_2_out_7));  // open: dp
endmodule

module ALU (
  input  in_1,
  input  in_2,
  input  a0,
  input  a1,
  input  a2,
  input  a3,
  input  sign_a,
  input  b0,
  input  b1,
  input  b2,
  input  b3,
  input  sign_b,
  output out_13,
  output out_14,
  output out_15,
  output out_16,
  output out_17,
  output out_18,
  output out_19,
  output out_20,
  output out_21,
  output Zero_Divider,
  output Sign_Flag
);

  wire addition_subtraction_1_out_12, addition_subtraction_1_out_13, addition_subtraction_1_out_14,
       addition_subtraction_1_out_15, addition_subtraction_1_out_16, addition_subtraction_1_out_17,
       addition_subtraction_1_out_18, addition_subtraction_1_out_19, addition_subtraction_1_sign,
       addition_subtraction_1_zero_flag, integer_division_1_d0, integer_division_1_d1, integer_division_1_d2,
       integer_division_1_d3, integer_division_1_out_15, integer_division_1_out_16,
       integer_division_1_out_17, integer_division_1_out_18, integer_division_1_sign,
       integer_division_1_zero_divider, integer_division_1_zero_input, multiplicator_with_flag_zero_1__1,
       multiplicator_with_flag_zero_1__2, multiplicator_with_flag_zero_1__3,
       multiplicator_with_flag_zero_1__4, multiplicator_with_flag_zero_1__5,
       multiplicator_with_flag_zero_1__6, multiplicator_with_flag_zero_1__7,
       multiplicator_with_flag_zero_1__8, multiplicator_with_flag_zero_1_sign_flag,
       multiplicator_with_flag_zero_1_zero_flag;

  Addition_Subtraction addition_subtraction_1 (
    .a0(a0), .a1(a1), .a2(a2), .a3(a3), .sign_a(sign_a), .b0(b0), .b1(b1), .b2(b2), .b3(b3), .sign_b(sign_b),
    .Mode(in_2), .out_12(addition_subtraction_1_out_12), .out_13(addition_subtraction_1_out_13),
    .out_14(addition_subtraction_1_out_14), .out_15(addition_subtraction_1_out_15),
    .out_16(addition_subtraction_1_out_16), .out_17(addition_subtraction_1_out_17),
    .out_18(addition_subtraction_1_out_18), .out_19(addition_subtraction_1_out_19),
    .Zero_Flag(addition_subtraction_1_zero_flag), .Sign(addition_subtraction_1_sign));
  multiplicator_with_flag_zero multiplicator_with_flag_zero_1 (
    .a0(a0), .a1(a1), .a2(a2), .a3(a3), .sigb_1(sign_a), .b0(b0), .b1(b1), .b2(b2), .b3(b3), .sign_2(sign_b),
    .zero_flag(multiplicator_with_flag_zero_1_zero_flag), ._8(multiplicator_with_flag_zero_1__8),
    ._7(multiplicator_with_flag_zero_1__7), ._6(multiplicator_with_flag_zero_1__6),
    ._5(multiplicator_with_flag_zero_1__5), ._4(multiplicator_with_flag_zero_1__4),
    .sign_flag(multiplicator_with_flag_zero_1_sign_flag), ._3(multiplicator_with_flag_zero_1__3),
    ._2(multiplicator_with_flag_zero_1__2), ._1(multiplicator_with_flag_zero_1__1));
  INTEGER_DIVISION integer_division_1 (
    .A_sign(sign_a), .b4(sign_b), .b1(b1), .b2(b2), .b3(b3), .a0(a0), .a1(a1), .a2(a2), .a3(a3), .b0(b0),
    .d0(integer_division_1_d0), .d1(integer_division_1_d1), .d2(integer_division_1_d2),
    .d3(integer_division_1_d3), .out_15(integer_division_1_out_15), .out_16(integer_division_1_out_16),
    .out_17(integer_division_1_out_17), .out_18(integer_division_1_out_18), .sign(integer_division_1_sign),
    .zero_divider(integer_division_1_zero_divider), .zero_input(integer_division_1_zero_input));
  Multiplexer multiplexer_1 (
    .in_3(addition_subtraction_1_zero_flag), .in_4(addition_subtraction_1_zero_flag),
    .in_5(multiplicator_with_flag_zero_1_zero_flag), .in_6(integer_division_1_zero_input), .in_1(in_1),
    .in_2(in_2), .out_7(out_21));
  Multiplexer multiplexer_2 (
    .in_3(addition_subtraction_1_out_12), .in_4(addition_subtraction_1_out_12),
    .in_5(multiplicator_with_flag_zero_1__1), .in_6(integer_division_1_d0), .in_1(in_1), .in_2(in_2),
    .out_7(out_13));
  Multiplexer multiplexer_3 (
    .in_3(addition_subtraction_1_out_13), .in_4(addition_subtraction_1_out_13),
    .in_5(multiplicator_with_flag_zero_1__2), .in_6(integer_division_1_d1), .in_1(in_1), .in_2(in_2),
    .out_7(out_14));
  Multiplexer multiplexer_4 (
    .in_3(1'b0), .in_4(1'b0), .in_5(1'b0), .in_6(integer_division_1_zero_divider), .in_1(in_1), .in_2(in_2),
    .out_7(Zero_Divider));
  Multiplexer multiplexer_5 (
    .in_3(addition_subtraction_1_out_14), .in_4(addition_subtraction_1_out_14),
    .in_5(multiplicator_with_flag_zero_1__3), .in_6(integer_division_1_d2), .in_1(in_1), .in_2(in_2),
    .out_7(out_15));
  Multiplexer multiplexer_6 (
    .in_3(addition_subtraction_1_out_15), .in_4(addition_subtraction_1_out_15),
    .in_5(multiplicator_with_flag_zero_1__4), .in_6(integer_division_1_d3), .in_1(in_1), .in_2(in_2),
    .out_7(out_16));
  Multiplexer multiplexer_7 (
    .in_3(addition_subtraction_1_sign), .in_4(addition_subtraction_1_sign),
    .in_5(multiplicator_with_flag_zero_1_sign_flag), .in_6(integer_division_1_sign), .in_1(in_1),
    .in_2(in_2), .out_7(Sign_Flag));
  Multiplexer multiplexer_8 (
    .in_3(addition_subtraction_1_out_16), .in_4(addition_subtraction_1_out_16),
    .in_5(multiplicator_with_flag_zero_1__5), .in_6(integer_division_1_out_15), .in_1(in_1), .in_2(in_2),
    .out_7(out_17));
  Multiplexer multiplexer_9 (
    .in_3(addition_subtraction_1_out_17), .in_4(addition_subtraction_1_out_17),
    .in_5(multiplicator_with_flag_zero_1__6), .in_6(integer_division_1_out_16), .in_1(in_1), .in_2(in_2),
    .out_7(out_18));
  Multiplexer multiplexer_10 (
    .in_3(addition_subtraction_1_out_18), .in_4(addition_subtraction_1_out_18),
    .in_5(multiplicator_with_flag_zero_1__7), .in_6(integer_division_1_out_17), .in_1(in_1), .in_2(in_2),
    .out_7(out_19));
  Multiplexer multiplexer_11 (
    .in_3(addition_subtraction_1_out_19), .in_4(addition_subtraction_1_out_19),
    .in_5(multiplicator_with_flag_zero_1__8), .in_6(integer_division_1_out_18), .in_1(in_1), .in_2(in_2),
    .out_7(out_20));

  // Notes on the sheet:
  //   Zero Flag
  //   Results
endmodule

module Multiplexer (
  input  in_1,
  input  in_2,
  input  in_3,
  input  in_4,
  input  in_5,
  input  in_6,
  output out_7
);

  wire and_1_out, and_2_out, and_3_out, and_4_out, and_5_out, and_6_out, and_7_out, and_8_out, not_1_out,
       not_2_out, or_1_out, or_2_out;

  not not_1 (not_1_out, in_1);
  not not_2 (not_2_out, in_2);
  and and_1 (and_1_out, not_2_out, not_1_out);
  and and_2 (and_2_out, in_2, not_1_out);
  and and_3 (and_3_out, not_2_out, in_1);
  and and_4 (and_4_out, in_2, in_1);
  and and_5 (and_5_out, and_1_out, in_3);
  and and_6 (and_6_out, and_2_out, in_4);
  and and_7 (and_7_out, and_3_out, in_5);
  and and_8 (and_8_out, and_4_out, in_6);
  or or_1 (or_1_out, and_5_out, and_6_out);
  or or_2 (or_2_out, or_1_out, and_7_out);
  or or_3 (out_7, or_2_out, and_8_out);
endmodule

module Demultiplexers (
  input  in_1,
  input  in_2,
  input  in_3,
  output out_4,
  output out_5,
  output out_6,
  output out_7
);

  wire and_1_out, and_2_out, and_3_out, and_4_out, not_1_out, not_2_out;

  not not_1 (not_1_out, in_1);
  not not_2 (not_2_out, in_2);
  and and_1 (and_1_out, not_2_out, not_1_out);
  and and_2 (and_2_out, in_2, not_1_out);
  and and_3 (and_3_out, not_2_out, in_1);
  and and_4 (and_4_out, in_2, in_1);
  and and_5 (out_4, and_1_out, in_3);
  and and_6 (out_5, and_2_out, in_3);
  and and_7 (out_6, and_3_out, in_3);
  and and_8 (out_7, and_4_out, in_3);
endmodule
